// Digital circuit ex2-0.dig as structural Verilog
module ex2_0 (
  input  [9:0] IN,
  output [2:0] OUT0,
  output [2:0] OUT1,
  output OUT2
);


  assign OUT0 = IN[2:0];
  assign OUT1 = IN[7:5];
  assign OUT2 = IN[8];

  // Notes on the sheet:
  //   IN: default 325
endmodule

/* Test case EX2-0 Test:
IN OUT0 OUT1 OUT2

 0b0111010101 0b101 0b110 1
 0b1000101010 0b010 0b001 0
*/
