// Digital circuit register-file.dig as structural Verilog
module register_file (
  input  [4:0] ReadReg1,
  input  [4:0] ReadReg2,
  input  [4:0] WriteReg,
  input  [31:0] WriteData,
  input  RegWrite,
  input  Clock,
  output [31:0] ReadData1,
  output [31:0] ReadData2
);

  wire decoder_1_out_0, decoder_1_out_1, decoder_1_out_2, decoder_1_out_3, decoder_1_out_4, decoder_1_out_5,
       decoder_1_out_6, decoder_1_out_7, decoder_1_out_8, decoder_1_out_9, decoder_1_out_10,
       decoder_1_out_11, decoder_1_out_12, decoder_1_out_13, decoder_1_out_14, decoder_1_out_15,
       decoder_1_out_16, decoder_1_out_17, decoder_1_out_18, decoder_1_out_19, decoder_1_out_20,
       decoder_1_out_21, decoder_1_out_22, decoder_1_out_23, decoder_1_out_24, decoder_1_out_25,
       decoder_1_out_26, decoder_1_out_27, decoder_1_out_28, decoder_1_out_29, decoder_1_out_30,
       decoder_1_out_31, en0, en1, en2, en3, en4, en5, en6, en7, en8, en9, en10, en11, en12, en13, en14,
       en15, en16, en17, en18, en19, en20, en21, en22, en23, en24, en25, en26, en27, en28, en29, en30, en31;
  wire [31:0] r0, r1, r2, r3, r4, r5, r6, r7, r8, r9, r10, r11, r12, r13, r14, r15, r16, r17, r18, r19, r20,
       r21, r22, r23, r24, r25, r26, r27, r28, r29, r30, r31;

  Register #(.Bits(32)) Reg_0 (.D(WriteData), .C(Clock), .en(en0), .Q(r0));
  Register #(.Bits(32)) Reg_8 (.D(WriteData), .C(Clock), .en(en8), .Q(r8));
  Register #(.Bits(32)) Reg_16 (.D(WriteData), .C(Clock), .en(en16), .Q(r16));
  Register #(.Bits(32)) Reg_24 (.D(WriteData), .C(Clock), .en(en24), .Q(r24));
  Decoder #(.Selector_Bits(5)) decoder_1 (
    .sel(WriteReg), .out_0(decoder_1_out_0), .out_1(decoder_1_out_1), .out_2(decoder_1_out_2),
    .out_3(decoder_1_out_3), .out_4(decoder_1_out_4), .out_5(decoder_1_out_5), .out_6(decoder_1_out_6),
    .out_7(decoder_1_out_7), .out_8(decoder_1_out_8), .out_9(decoder_1_out_9), .out_10(decoder_1_out_10),
    .out_11(decoder_1_out_11), .out_12(decoder_1_out_12), .out_13(decoder_1_out_13),
    .out_14(decoder_1_out_14), .out_15(decoder_1_out_15), .out_16(decoder_1_out_16),
    .out_17(decoder_1_out_17), .out_18(decoder_1_out_18), .out_19(decoder_1_out_19),
    .out_20(decoder_1_out_20), .out_21(decoder_1_out_21), .out_22(decoder_1_out_22),
    .out_23(decoder_1_out_23), .out_24(decoder_1_out_24), .out_25(decoder_1_out_25),
    .out_26(decoder_1_out_26), .out_27(decoder_1_out_27), .out_28(decoder_1_out_28),
    .out_29(decoder_1_out_29), .out_30(decoder_1_out_30), .out_31(decoder_1_out_31));
  Register #(.Bits(32)) Reg_1 (.D(WriteData), .C(Clock), .en(en1), .Q(r1));
  Register #(.Bits(32)) Reg_9 (.D(WriteData), .C(Clock), .en(en9), .Q(r9));
  Register #(.Bits(32)) Reg_17 (.D(WriteData), .C(Clock), .en(en17), .Q(r17));
  Register #(.Bits(32)) Reg_25 (.D(WriteData), .C(Clock), .en(en25), .Q(r25));
  Register #(.Bits(32)) Reg_2 (.D(WriteData), .C(Clock), .en(en2), .Q(r2));
  Register #(.Bits(32)) Reg_10 (.D(WriteData), .C(Clock), .en(en10), .Q(r10));
  Register #(.Bits(32)) Reg_18 (.D(WriteData), .C(Clock), .en(en18), .Q(r18));
  Register #(.Bits(32)) Reg_26 (.D(WriteData), .C(Clock), .en(en26), .Q(r26));
  and and_1 (en0, 1'b0, decoder_1_out_0);
  Register #(.Bits(32)) Reg_3 (.D(WriteData), .C(Clock), .en(en3), .Q(r3));
  Register #(.Bits(32)) Reg_11 (.D(WriteData), .C(Clock), .en(en11), .Q(r11));
  Register #(.Bits(32)) Reg_19 (.D(WriteData), .C(Clock), .en(en19), .Q(r19));
  Register #(.Bits(32)) Reg_27 (.D(WriteData), .C(Clock), .en(en27), .Q(r27));
  Register #(.Bits(32)) Reg_4 (.D(WriteData), .C(Clock), .en(en4), .Q(r4));
  Register #(.Bits(32)) Reg_12 (.D(WriteData), .C(Clock), .en(en12), .Q(r12));
  Register #(.Bits(32)) Reg_20 (.D(WriteData), .C(Clock), .en(en20), .Q(r20));
  Register #(.Bits(32)) Reg_28 (.D(WriteData), .C(Clock), .en(en28), .Q(r28));
  Register #(.Bits(32)) Reg_5 (.D(WriteData), .C(Clock), .en(en5), .Q(r5));
  Register #(.Bits(32)) Reg_13 (.D(WriteData), .C(Clock), .en(en13), .Q(r13));
  Register #(.Bits(32)) Reg_21 (.D(WriteData), .C(Clock), .en(en21), .Q(r21));
  Register #(.Bits(32)) Reg_29 (.D(WriteData), .C(Clock), .en(en29), .Q(r29));
  Register #(.Bits(32)) Reg_6 (.D(WriteData), .C(Clock), .en(en6), .Q(r6));
  Register #(.Bits(32)) Reg_14 (.D(WriteData), .C(Clock), .en(en14), .Q(r14));
  Register #(.Bits(32)) Reg_22 (.D(WriteData), .C(Clock), .en(en22), .Q(r22));
  Register #(.Bits(32)) Reg_30 (.D(WriteData), .C(Clock), .en(en30), .Q(r30));
  and and_2 (en1, decoder_1_out_1, RegWrite);
  and and_3 (en2, decoder_1_out_2, RegWrite);
  and and_4 (en3, decoder_1_out_3, RegWrite);
  and and_5 (en4, decoder_1_out_4, RegWrite);
  and and_6 (en5, decoder_1_out_5, RegWrite);
  and and_7 (en6, decoder_1_out_6, RegWrite);
  and and_8 (en7, decoder_1_out_7, RegWrite);
  and and_9 (en8, decoder_1_out_8, RegWrite);
  and and_10 (en9, decoder_1_out_9, RegWrite);
  and and_11 (en10, decoder_1_out_10, RegWrite);
  and and_12 (en11, decoder_1_out_11, RegWrite);
  and and_13 (en12, decoder_1_out_12, RegWrite);
  and and_14 (en13, decoder_1_out_13, RegWrite);
  and and_15 (en14, decoder_1_out_14, RegWrite);
  and and_16 (en15, decoder_1_out_15, RegWrite);
  and and_17 (en16, decoder_1_out_16, RegWrite);
  and and_18 (en17, decoder_1_out_17, RegWrite);
  and and_19 (en18, decoder_1_out_18, RegWrite);
  and and_20 (en19, decoder_1_out_19, RegWrite);
  and and_21 (en20, decoder_1_out_20, RegWrite);
  and and_22 (en21, decoder_1_out_21, RegWrite);
  and and_23 (en22, decoder_1_out_22, RegWrite);
  and and_24 (en23, decoder_1_out_23, RegWrite);
  and and_25 (en24, decoder_1_out_24, RegWrite);
  and and_26 (en25, decoder_1_out_25, RegWrite);
  and and_27 (en26, decoder_1_out_26, RegWrite);
  and and_28 (en27, decoder_1_out_27, RegWrite);
  and and_29 (en28, decoder_1_out_28, RegWrite);
  and and_30 (en29, decoder_1_out_29, RegWrite);
  and and_31 (en30, decoder_1_out_30, RegWrite);
  and and_32 (en31, decoder_1_out_31, RegWrite);
  Register #(.Bits(32)) Reg_7 (.D(WriteData), .C(Clock), .en(en7), .Q(r7));
  Register #(.Bits(32)) Reg_15 (.D(WriteData), .C(Clock), .en(en15), .Q(r15));
  Register #(.Bits(32)) Reg_23 (.D(WriteData), .C(Clock), .en(en23), .Q(r23));
  Register #(.Bits(32)) Reg_31 (.D(WriteData), .C(Clock), .en(en31), .Q(r31));
  Multiplexer #(.Bits(32), .Selector_Bits(5)) multiplexer_1 (
    .sel(ReadReg1), .in_0(r0), .in_1(r1), .in_2(r2), .in_3(r3), .in_4(r4), .in_5(r5), .in_6(r6), .in_7(r7),
    .in_8(r8), .in_9(r9), .in_10(r10), .in_11(r11), .in_12(r12), .in_13(r13), .in_14(r14), .in_15(r15),
    .in_16(r16), .in_17(r17), .in_18(r18), .in_19(r19), .in_20(r20), .in_21(r21), .in_22(r22), .in_23(r23),
    .in_24(r24), .in_25(r25), .in_26(r26), .in_27(r27), .in_28(r28), .in_29(r29), .in_30(r30), .in_31(r31),
    .out(ReadData1));
  Multiplexer #(.Selector_Bits(5), .Bits(32)) multiplexer_2 (
    .sel(ReadReg2), .in_0(r0), .in_1(r1), .in_2(r2), .in_3(r3), .in_4(r4), .in_5(r5), .in_6(r6), .in_7(r7),
    .in_8(r8), .in_9(r9), .in_10(r10), .in_11(r11), .in_12(r12), .in_13(r13), .in_14(r14), .in_15(r15),
    .in_16(r16), .in_17(r17), .in_18(r18), .in_19(r19), .in_20(r20), .in_21(r21), .in_22(r22), .in_23(r23),
    .in_24(r24), .in_25(r25), .in_26(r26), .in_27(r27), .in_28(r28), .in_29(r29), .in_30(r30), .in_31(r31),
    .out(ReadData2));

  // Other names for the same wires on the sheet: clk = Clock; rr1[4:0] = ReadReg1; rr2[4:0] = ReadReg2; rw = RegWrite;
  //   wd[31:0] = WriteData; wr[4:0] = WriteReg
endmodule

/* Test case Register File Test:
WriteReg WriteData RegWrite Clock ReadReg1 ReadReg2 ReadData1 ReadData2

# $1 = 25
1 25 1 C 1 0 25 0

# $2 = 30
2 30 1 C 0 2 0 30

# $(N+1) = (N+1)
loop(N, 30)
	(N+1) (N+1) 1 C (N+1) (N) (N+1) (N)
end loop

# $(N+1) = N-60
loop(N, 30)
	(N+1) (N-60) 1 C (N+1) (N+1) (N-60) (N-60)
end loop

# Try writing to $0. This should not write anything
0 25 1 C 0 0 0 0

# try writing when RegWrite = 0
# (the registers should still have their old values)
loop(N, 30)
	(N+1) (N+80) 0 C (N+1) (N+1) (N-60) (N-60)
end loop
*/
