// Digital circuit control-unit.dig as structural Verilog
module control_unit (
  input  [6:0] opcode,
  input  [2:0] funct3,
  input  [6:0] funct7,
  output RegWrite,
  output ALUSrc,
  output [1:0] ImmSrc,
  output [3:0] ALUOperation
);

  wire funct3_2_eq, funct3_3_eq, funct3_4_eq, funct3_5_eq, funct3_6_eq, funct3_7_eq, funct3_8_eq, funct3_eq,
       funct7_2_eq, funct7_3_eq, funct7_4_eq, funct7_5_eq, funct7_eq, is_add, is_addi, is_and, is_andi,
       is_or, is_slt, is_slti, is_sub, opcode_2_eq, opcode_3_eq, opcode_4_eq, opcode_5_eq, opcode_6_eq,
       opcode_7_eq, opcode_8_eq, opcode_eq;
  wire [2:0] priorityencoder_1_num;

  Comparator #(.Bits(7)) u_opcode (.a(opcode), .b(7'b0110011), .eq(opcode_eq));  // open: gt, lt
  Comparator #(.Bits(3)) u_funct3 (.a(funct3), .b(3'b000), .eq(funct3_eq));  // open: gt, lt
  Comparator #(.Bits(7)) u_funct7 (.a(funct7), .b({7{1'b0}}), .eq(funct7_eq));  // open: gt, lt
  Comparator #(.Bits(7)) opcode_2 (.a(opcode), .b(7'b0110011), .eq(opcode_2_eq));  // open: gt, lt
  Comparator #(.Bits(3)) funct3_2 (.a(funct3), .b(3'b000), .eq(funct3_2_eq));  // open: gt, lt
  Comparator #(.Bits(7)) funct7_2 (.a(funct7), .b(7'b0100000), .eq(funct7_2_eq));  // open: gt, lt
  and and_1 (is_add, opcode_eq, funct3_eq, funct7_eq);
  and and_2 (is_sub, opcode_2_eq, funct3_2_eq, funct7_2_eq);
  Comparator #(.Bits(7)) opcode_3 (.a(opcode), .b(7'b0110011), .eq(opcode_3_eq));  // open: gt, lt
  Comparator #(.Bits(3)) funct3_3 (.a(funct3), .b(3'b111), .eq(funct3_3_eq));  // open: gt, lt
  Comparator #(.Bits(7)) funct7_3 (.a(funct7), .b({7{1'b0}}), .eq(funct7_3_eq));  // open: gt, lt
  PriorityEncoder #(.Selector_Bits(3)) priorityencoder_1 (
    .in0(is_add), .in1(is_sub), .in2(is_and), .in3(is_or), .in4(is_slt), .in5(is_addi), .in6(is_slti),
    .in7(is_andi), .num(priorityencoder_1_num));  // open: any
  and and_3 (is_and, opcode_3_eq, funct3_3_eq, funct7_3_eq);
  Comparator #(.Bits(7)) opcode_4 (.a(opcode), .b(7'b0110011), .eq(opcode_4_eq));  // open: gt, lt
  Comparator #(.Bits(3)) funct3_4 (.a(funct3), .b(3'b110), .eq(funct3_4_eq));  // open: gt, lt
  Comparator #(.Bits(7)) funct7_4 (.a(funct7), .b({7{1'b0}}), .eq(funct7_4_eq));  // open: gt, lt
  Comparator #(.Bits(7)) opcode_5 (.a(opcode), .b(7'b0110011), .eq(opcode_5_eq));  // open: gt, lt
  Comparator #(.Bits(3)) funct3_5 (.a(funct3), .b(3'b010), .eq(funct3_5_eq));  // open: gt, lt
  Comparator #(.Bits(7)) funct7_5 (.a(funct7), .b({7{1'b0}}), .eq(funct7_5_eq));  // open: gt, lt
  and and_4 (is_or, opcode_4_eq, funct3_4_eq, funct7_4_eq);
  and and_5 (is_slt, opcode_5_eq, funct3_5_eq, funct7_5_eq);
  ROM #(.AddrBits(3), .Bits(8)) rom_1 (
    .A(priorityencoder_1_num), .sel(1'b1), .D({RegWrite, ALUSrc, ImmSrc, ALUOperation}));
  Comparator #(.Bits(7)) opcode_6 (.a(opcode), .b(7'b0010011), .eq(opcode_6_eq));  // open: gt, lt
  Comparator #(.Bits(3)) funct3_6 (.a(funct3), .b(3'b000), .eq(funct3_6_eq));  // open: gt, lt
  Comparator #(.Bits(7)) opcode_7 (.a(opcode), .b(7'b0010011), .eq(opcode_7_eq));  // open: gt, lt
  Comparator #(.Bits(3)) funct3_7 (.a(funct3), .b(3'b010), .eq(funct3_7_eq));  // open: gt, lt
  Comparator #(.Bits(7)) opcode_8 (.a(opcode), .b(7'b0010011), .eq(opcode_8_eq));  // open: gt, lt
  Comparator #(.Bits(3)) funct3_8 (.a(funct3), .b(3'b111), .eq(funct3_8_eq));  // open: gt, lt
  and and_6 (is_addi, opcode_6_eq, funct3_6_eq);
  and and_7 (is_slti, opcode_7_eq, funct3_7_eq);
  and and_8 (is_andi, opcode_8_eq, funct3_8_eq);

  // Notes on the sheet:
  //   R-Type is_X
  //   is_add
  //   is_sub
  //   Inputs
  //   is_and
  //   Outputs
  //   is_or
  //   is_slt
  //   contents of rom_1 (hex, n*v repeats v):
  //   82,86,80,81,87,c2,c7,c0
  //   I-Type is_X
  //   is_addi
  //   is_slti
  //   is_andi
endmodule

/* Test case cpu test:
opcode funct3 funct7 ALUOperation ImmSrc ALUSrc RegWrite

# ----------- R-Type tests (opcode = 0b0110011)-----------

#add
0b0110011 0b000 0b0000000 0b0010 0b00 0b0 0b1
#sub
0b0110011 0b000 0b0100000 0b0110 0b00 0b0 0b1
#and
0b0110011 0b111 0b0000000 0b0000 0b00 0b0 0b1
#or
0b0110011 0b110 0b0000000 0b0001 0b00 0b0 0b1
#slt
0b0110011 0b010 0b0000000 0b0111 0b00 0b0 0b1

#----------- I-type ALU (opcode = 0010011)-----------

#addi
0b0010011 0b000 0b0000000 0b0010 0b00 0b1 0b1
#slti
0b0010011 0b010 0b0000000 0b0111 0b00 0b1 0b1
#andi
0b0010011 0b111 0b0000000 0b0000 0b00 0b1 0b1
*/
